# Fritzing sketch IOT (saved by Fritzing 0.9.3b)
breadboards: 1

parts:
  R1 = Resistor [tolerance=±5% resistance=220 package=THT]
  R2 = Resistor [tolerance=±5% resistance=220 package=THT]
  Composant1 = Arduino Uno (Rev3)
  LCD1 = LCD screen
  DHT1 = DHT11 Humitidy and Temperature Sensor
  R3 = PHOTOCELL [package=photocell]
  U1 = HIH-4030 [package=hih-4030]
  U2 = POT_SWITCH [package=pot_pth_switch]

nets:
  VDD: R1.Pin_0, Composant1.5V, LCD1.VDD, DHT1.VDD, R3.P$1, U1.VCC, U2.G$2_2
  N1: R1.Pin_1, LCD1.LED+
  N2: R2.Pin_0, Composant1.A1, R3.P$2
  N3: Composant1.A0, U1.OUT
  N4: Composant1.D10_PWM/SS, DHT1.DATA
  N5: Composant1.D11_PWM/MOSI, LCD1.E
  N6: Composant1.D12/MISO, LCD1.RS
  N7: Composant1.D2, LCD1.DB7
  N8: Composant1.D3_PWM, LCD1.DB6
  N9: Composant1.D4, LCD1.DB5
  N10: Composant1.D5_PWM, LCD1.DB4
  GND: Composant1.GND, LCD1.VSS, LCD1.R/W, LCD1.LED-, DHT1.GND, U1.GND, U2.G$1_A
  N11: LCD1.V0, U2.G$2_1

custom parts:
  DHT11 Humitidy and Temperature Sensor: DHT11 Humidity and Temperature Sensor
